# Fritzing sketch wheater2 (saved by Fritzing 0.9.3b)

parts:
  Bauteil1 = Arduino Nano (Rev3.0)
  LCD1 = LCD screen
  VCC1 = Battery
  S1 = Toggle Switch [package=THT]
  R1 = Resistor [tolerance=±5% resistance=220 package=THT]
  Q1 = NPN-Transistor [package="TO92 [THT]"]
  S2 = Square Pushbutton
  Bauteil2 = BME280 Breakout

nets:
  GND: Bauteil1.GND, VCC1.-, Q1.E, S2.leg0, Bauteil2.GND
  N1: Bauteil1.D3, LCD1.DB4
  N2: Bauteil1.D4, LCD1.DB5
  N3: Bauteil1.D5, LCD1.DB6
  N4: Bauteil1.D6, LCD1.DB7
  N5: Bauteil1.D7, LCD1.E
  N6: Bauteil1.D8, LCD1.RS
  N7: Bauteil1.D9, R1.Pin_0
  N8: Bauteil1.D10, S2.leg1
  5V: Bauteil1.5V, LCD1.VDD, LCD1.LED+, S1.L2, Bauteil2.3.3V
  N9: Bauteil1.A5, Bauteil2.SCK/SCL
  N10: Bauteil1.A4, Bauteil2.SDI/SDA
  N11: LCD1.VSS, LCD1.V0, LCD1.R/W
  N12: LCD1.LED-, Q1.C
  N13: VCC1.+, S1.COM
  N14: R1.Pin_1, Q1.B
